# Fritzing sketch ReactiveMotor_Annex (saved by Fritzing 0.9.3b)
circuit board: 9.97452cm x 10.6314cm
breadboards: 1

parts:
  REG_AD588BQ = IC, DIP package, 16 pins [chip_label=REG part_number=AD588BQ]
  LS1 = TXB0104 4-channel Bi-Directional Level Shifter
  LS2 = TXB0104 4-channel Bi-Directional Level Shifter
  ADC_ADS7813 = IC, DIP package, 16 pins [chip_label=ADC part_number=ADS7813]
  DAC_AD7849CN = IC, DIP package, 20 pins [chip_label=DAC part_number=AD7849CN]
  J3 = screw terminal, 3 pins
  J4 = screw terminal, 3 pins
  J2 = screw terminal, 3 pins
  J5 = screw terminal, 3 pins
  R3 = Resistor [tolerance=±5% resistance=39k package=THT]
  C1 = Ceramic Capacitor [capacitance=1µF package="100 mil [THT, multilayer]"]
  C3 = Ceramic Capacitor [capacitance=1µF package="100 mil [THT, multilayer]"]
  C4 = Electrolytic Capacitor [capacitance=1µF package="100 mil [THT, electrolytic]"]
  C5 = Electrolytic Capacitor [capacitance=1µF package="100 mil [THT, electrolytic]"]
  C6 = Ceramic Capacitor [capacitance=100nF package="100 mil [THT, multilayer]"]
  C7 = Electrolytic Capacitor [capacitance=10µF package="100 mil [THT, electrolytic]"]
  R2 = Rotary Potentiometer (Large) [maximum_resistance=100kΩ package=THT]
  R1 = Rotary Potentiometer (Large) [maximum_resistance=100kΩ package=THT]
  J6 = double row female pin header, 12 pins [form="♀ (female)"]

nets:
  N1: REG_AD588BQ.pin1, REG_AD588BQ.pin3, DAC_AD7849CN.pin1
  N2: REG_AD588BQ.pin2, DAC_AD7849CN.pin17, J4.pin1, R3.Pin_0, R2.leg1, R1.leg1
  N3: REG_AD588BQ.pin4, REG_AD588BQ.pin6, R3.Pin_1
  N4: REG_AD588BQ.pin5, R1.wiper
  N5: REG_AD588BQ.pin7, C1.1
  N6: REG_AD588BQ.pin8, REG_AD588BQ.pin13, R2.leg2, R1.leg2
  GND: REG_AD588BQ.pin9, LS1.GND, LS2.GND, ADC_ADS7813.pin2, ADC_ADS7813.pin4, ADC_ADS7813.pin8, ADC_ADS7813.pin15, DAC_AD7849CN.pin8, DAC_AD7849CN.pin9, DAC_AD7849CN.pin10, DAC_AD7849CN.pin11, DAC_AD7849CN.pin16, DAC_AD7849CN.pin20, J3.pin3, J2.pin3, J5.pin3, C1.0, C3.1, C4.-, C5.-, C6.1, C7.-
  N7: REG_AD588BQ.pin10, REG_AD588BQ.pin11
  N8: REG_AD588BQ.pin12, R2.wiper
  N9: REG_AD588BQ.pin14, REG_AD588BQ.pin15, DAC_AD7849CN.pin2
  N10: REG_AD588BQ.pin16, DAC_AD7849CN.pin3, J4.pin3
  N11: LS1.HV, LS2.HV, ADC_ADS7813.pin11, ADC_ADS7813.pin16, DAC_AD7849CN.pin6, DAC_AD7849CN.pin13, DAC_AD7849CN.pin14, J3.pin1, C6.0, C7.+
  N12: LS1.B1, ADC_ADS7813.pin13
  N13: LS1.B2, ADC_ADS7813.pin14
  N14: LS1.B3, DAC_AD7849CN.pin12
  N15: LS1.OE, J6.pin7
  N16: LS1.A3, J6.pin9
  N17: LS1.A2, J6.pin10
  N18: LS1.A1, J6.pin11
  N19: LS1.LV, J6.pin12
  N20: LS2.B1, ADC_ADS7813.pin9, DAC_AD7849CN.pin5
  N21: LS2.B2, ADC_ADS7813.pin10
  N22: LS2.B3, DAC_AD7849CN.pin4
  N23: LS2.B4, ADC_ADS7813.pin12
  N24: LS2.OE, J6.pin1
  N25: LS2.A4, J6.pin2
  N26: LS2.A3, J6.pin3
  N27: LS2.A2, J6.pin4
  N28: LS2.A1, J6.pin5
  N29: LS2.LV, J6.pin6
  N30: ADC_ADS7813.pin1, J2.pin1
  N31: ADC_ADS7813.pin3, ADC_ADS7813.pin5
  N32: ADC_ADS7813.pin6, C3.0, C4.+
  N33: ADC_ADS7813.pin7, C5.+
  N34: DAC_AD7849CN.pin19, J5.pin1

notes:
  -15V
  +15V
  GND
  +5V
  FOUT
  +/-5V REG
  DAC
  ADC
  LIN
  AD588BQ
  AD7849CN
  ADS7813
  1uF
  39k
  1
  3
  2
  10nF
  10uF
  100nF
  3.3V
  SCLK
  ADC DATA
  DAC !SYNC
  DAC SDIN
  ADC !CS
  ADC !BUSY
  ADC !CONV

custom parts:
  TXB0104 4-channel Bi-Directional Level Shifter: Because the Arduino (and Basic Stamp) are 5V devices, and most modern sensors, displays, flash cards and modes are 3.3V-only, many makers find that they need to perform level shifting/conversion to protect the 3.3V device from 5V. Although one can use resistors to make a divider, for high speed transfers, the resistors can add a lot of slew and cause havoc that is tough to debug. For that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
