# Fritzing sketch ReactiveMotor_Cape (saved by Fritzing 0.9.3b)
circuit board: 6.5279cm x 5.98907cm
perfboards: 1

parts:
  LED1 = LED - 5mm [color="Red (633nm)" package="5 mm [THT]"]
  R1 = Resistor [tolerance=±5% resistance=680 package=THT]
  J6 = double row female pin header, 12 pins [form="♀ (female)"]
  J7 = double row male pin header, 10 pins [form="♂ (male)"]
  J4 = double row male pin header, 24 pins [form="♂ (male)"]
  J2 = double row male pin header, 46 pins [form="♂ (male)"]
  S1 = Pushbutton [package="[THT]"]

nets:
  N1: LED1.cathode, R1.Pin_1
  N2: LED1.anode, J2.pin6
  N3: R1.Pin_0, J2.pin1
  N4: J6.pin1, J4.pin24
  N5: J6.pin3, J4.pin16
  N6: J6.pin4, J4.pin19
  N7: J6.pin5, J4.pin7
  N8: J6.pin6, J6.pin12, J4.pin2, S1.Pin_1, S1.Pin_2
  N9: J6.pin7, J7.pin6
  N10: J6.pin8, J4.pin6
  N11: J6.pin9, J4.pin9
  N12: J6.pin10, J4.pin11
  N13: J6.pin11, J4.pin14
  N14: J7.pin2, S1.Pin_3, S1.Pin_4

notes:
  ADC !CONV
  ADC !BUSY
  ADC !CS
  DAC SDIN
  DAC !SYNC
  ADC DATA
  SCLK
  3.3V
  GND
